# Fritzing sketch Blinking LED (saved by Fritzing 0.9.2b)
breadboards: 1

parts:
  Part1 = Arduino Mega 2560 (Rev3)
  R1 = Resistor [tolerance=±5% resistance=220 package=THT]
  LED1 = smd LED [color="Red (633nm)" package="0805 [SMD]"]

nets:
  N1: Part1.GND, LED1.anode
  N2: Part1.D13_PWM, R1.Pin_1
  N3: R1.Pin_0, LED1.cathode
