# Fritzing sketch Untitled Sketch (saved by Fritzing 0.9.2b)
breadboards: 1

parts:
  Part1 = Arduino Mega 2560 (Rev3)
  S1 = Momentary Switch [package=ksa_sealed_tac_switch]
  R1 = Resistor [tolerance=±5% resistance=220 package="0402 [SMD]"]
  LCD1 = LCD screen

nets:
  N1: Part1.D10_PWM, LCD1.DB7
  N2: Part1.D9_PWM, LCD1.DB6
  N3: Part1.D8_PWM, LCD1.DB5
  5V: Part1.5V, S1.3, LCD1.VDD, LCD1.LED+
  GND: Part1.GND, R1.Pin_0, LCD1.VSS, LCD1.R/W, LCD1.LED-
  N4: Part1.D5_PWM, LCD1.RS
  N5: Part1.D6_PWM, LCD1.E
  N6: Part1.D7_PWM, LCD1.DB4
